# Fritzing sketch RC_Car (saved by Fritzing 0.9.3b)
breadboards: 2

parts:
  VCC1 = Battery block 9V
  VCC2 = 4 x AAA Battery Mount
  U1 = L9110 H-bridge module [part_number="L9110 H-bridge"]
  M2 = DC Motor
  U4 = HC-SR04 [chip_label=IC package="SIP (Single Inline) [THT]"]
  LED1 = LED - 5mm [color="Red (633nm)" package="5 mm [THT]"]
  부품2 = Bluetooth HC-06
  S1 = SWITCH-DPDT-latching [package=os]
  부품1 = Arduino Nano (Rev3.0)
  U3 = HC-SR04 [chip_label=IC package="SIP (Single Inline) [THT]"]
  LED2 = LED - 5mm [color="Red (633nm)" package="5 mm [THT]"]
  M1 = DC Motor

nets:
  N1: VCC1.-, VCC2.-, S1.3, S1.4
  VIN: VCC1.+, 부품1.VIN, U3.Vcc
  VCC: VCC2.+, U1.VCC, U4.Vcc, 부품2.VCC
  N2: U1.B-IA, 부품1.D5
  N3: U1.B-IB, 부품1.D6
  GND: U1.GND, U4.GND, LED1.cathode, 부품2.GND, S1.2, S1.5, 부품1.GND, U3.GND, LED2.cathode
  N4: U1.A-IA, 부품1.D3
  N5: U1.A-IB, 부품1.D11/MOSI
  N6: U1.MOTOR_A-A, M1.pin_1
  N7: U1.MOTOR_A-B, M1.pin_2
  N8: U1.MOTOR_B-A, M2.pin_2
  N9: U1.MOTOR_B-B, M2.pin_1
  N10: U4.Trig, 부품1.D8
  N11: U4.Echo, 부품1.D9
  N12: LED1.anode, 부품1.D4, LED2.anode
  N13: 부품2.RXD, 부품1.D1/TX
  N14: 부품2.TXD, 부품1.D0/RX
  N15: S1.1, S1.6
  N16: 부품1.D7, U3.Trig
  N17: 부품1.D10, U3.Echo

custom parts:
  HC-SR04: HC-SR04 ultrasound distance sensor
  SWITCH-DPDT-latching: DPDT latching pushbutton switch
